# Fritzing sketch Untitled Sketch (saved by Fritzing 1.0.6)
breadboards: 1

parts:
  Part1 = Arduino Mega ADK (Rev3)
  M4 = gear-motor
  M5 = gear-motor
  M6 = gear-motor
  M7 = gear-motor
  J1 = Basic Servo
  BAT1 = Battery Holders [package=battery-aaa]
  BAT2 = Battery Holders [package=battery-aaa]
  Q1 = NPN-Transistor [package="TO92 [THT]"]
  C1 = Capacitor [package=cap-pth-small2]
  R1 = Resistor [tolerance=±5% resistance=220 package="2512 [SMD]"]
  D1 = Diode [package=diode-1n4148]
  L298N1 = L298N DC motor driver
  S1 = KY-026
  S2 = KY-026
  S3 = KY-026
  S4 = SPST Switch [package=switche-dpdt]
  Mini_Water_Pump_3-6VDC1 = Mini Water Pump 3-6VDC [part_number="Mini Water Pump 3-6VDC" chip_label=IC package="DIP (Dual Inline) [THT]"]

nets:
  N1: Part1.A1, S3.pin1
  N2: Part1.A4, J1.pulse
  N3: Part1.A5, R1.Pin_1
  N4: Part1.D10_PWM, L298N1.ENB
  N5: Part1.D9_PWM, L298N1.IN4
  N6: Part1.D8_PWM, L298N1.IN3
  N7: Part1.5V, S1.pin1
  GND: Part1.GND, Q1.E, L298N1.GND, S2.pin1
  VIN: Part1.VIN, C1.2, D1.A, L298N1.12V, Mini_Water_Pump_3-6VDC1.-M
  N8: Part1.D5_PWM, L298N1.ENA
  N9: Part1.D6_PWM, L298N1.IN1
  N10: Part1.D7_PWM, L298N1.IN2
  N11: M4.pin_1, M7.pin_1, L298N1.OUT4
  N12: M4.pin_2, M7.pin_2, L298N1.OUT3
  N13: M5.pin_1, M6.pin_1, L298N1.OUT1
  N14: M5.pin_2, M6.pin_2, L298N1.OUT2
  N15: BAT1.-, BAT2.-, S4.O
  N16: BAT1.+, BAT2.+, S4.S
  N17: Q1.B, C1.1, D1.C, Mini_Water_Pump_3-6VDC1.+M
  N18: Q1.C, R1.Pin_0
  N19: S1.pin2, S3.pin2
  N20: S1.pin3, S3.pin3

custom parts:
  L298N DC motor driver: 2x DC motor driver with 78M05 positive voltage regulator (7..35 V) L298N: max 46 V, 2 A Set 5 V Enable jumper to enable 5 V regultor (needed for the L298N) and +5 V output at screw terminal or supply external +5 V at screw terminal Set ENA and/or ENB to +5 V to enable motor permanently or supply ENA and/or ENB with PWM signal IN1 and IN2 set rotation directory for motor A (OUT1/OUT2) IN2 and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
  KY-026: ky-026 flame sensor module
